// Logisim project datapath.circ as structural Verilog: 8 circuits, main circuit main
module main (
  input  [31:0] in_1,
  input  W_EN
);

  wire alu_1_neg, alu_1_zero, clk_out, CU_mux_br, CU_mux_br_fine, CU_mux_mem_in, CU_mux_pc_in, CU_pc_w_en,
       CU_w_en_a, CU_w_en_b, CU_w_en_mem, CU_w_en_sp, rst_2_out, RST_out;
  wire [1:0] CU_alu_sel, CU_mux_a_in, CU_mux_alu_a, CU_mux_alu_b;
  wire [31:0] A_out, adder_1_out, alu_1_out, B_out, CU_imm, multiplexer_1_out, multiplexer_2_out,
       multiplexer_3_out, multiplexer_4_out, multiplexer_5_out, multiplexer_6_out, multiplexer_7_out,
       multiplexer_8_out, multiplexer_9_out, PC_out, ram_1_data, ram_2_data, SP_out;

  Multiplexer #(.width(32), .enable("false")) multiplexer_1 (
    .in0(adder_1_out), .in1(alu_1_out), .out(multiplexer_1_out), .sel(CU_mux_pc_in));
  Adder #(.width(32)) adder_1 (.a(PC_out), .b(multiplexer_2_out), .out(adder_1_out));  // open: cin, cout
  register PC (.in(multiplexer_1_out), .clk(clk_out), .wen(CU_pc_w_en), .out(PC_out), .rst(rst_2_out));
  Multiplexer #(.width(32), .enable("false")) multiplexer_2 (
    .in0(32'h1), .in1(multiplexer_7_out), .out(multiplexer_2_out), .sel(CU_mux_br));
  Button RST (.out(RST_out));
  Multiplexer #(.select(2), .width(32), .enable("false")) multiplexer_3 (
    .in0(PC_out), .in1(ram_2_data), .in2(alu_1_out), .in3(B_out), .out(multiplexer_3_out), .sel(CU_mux_a_in));
  register A (.in(multiplexer_3_out), .clk(clk_out), .wen(CU_w_en_a), .out(A_out), .rst(rst_2_out));
  register B (.in(A_out), .clk(clk_out), .wen(CU_w_en_b), .out(B_out), .rst(rst_2_out));
  register SP (.in(alu_1_out), .clk(clk_out), .wen(CU_w_en_sp), .out(SP_out), .rst(rst_2_out));
  Button rst_2 (.out(rst_2_out));
  Clock clk (.out(clk_out));
  RAM #(.addrWidth(16), .dataWidth(32), .bus("separate")) ram_1 (
    .addr(PC_out[15:0]), .din(in_1), .data(ram_1_data), .str(W_EN), .sel(1'b1), .clk(clk_out), .ld(1'b1),
    .clr(RST_out));
  Multiplexer #(.select(2), .width(32), .enable("false")) multiplexer_4 (
    .in0(PC_out), .in1(A_out), .in2(SP_out), .in3({32{1'b0}}), .out(multiplexer_4_out), .sel(CU_mux_alu_a));
  Multiplexer #(.select(2), .width(32), .enable("false")) multiplexer_5 (
    .in0(CU_imm), .in1(B_out), .in2({32{1'b0}}), .in3(A_out), .out(multiplexer_5_out), .sel(CU_mux_alu_b));
  Multiplexer #(.width(32), .enable("false")) multiplexer_6 (
    .in0(32'h1), .in1(CU_imm), .out(multiplexer_6_out), .sel(alu_1_zero));
  Multiplexer #(.width(32), .enable("false")) multiplexer_7 (
    .in0(multiplexer_6_out), .in1(multiplexer_8_out), .out(multiplexer_7_out), .sel(CU_mux_br_fine));
  Multiplexer #(.width(32), .enable("false")) multiplexer_8 (
    .in0(32'h1), .in1(CU_imm), .out(multiplexer_8_out), .sel(alu_1_neg));
  alu alu_1 (
    .code(CU_alu_sel), .Out(alu_1_out), .Zero(alu_1_zero), .Neg(alu_1_neg), .A(multiplexer_4_out),
    .B(multiplexer_5_out));
  control_unit CU (
    .MUX_MEM_IN(CU_mux_mem_in), .W_EN_MEM(CU_w_en_mem), .MUX_ALU_B(CU_mux_alu_b), .MUX_A_IN(CU_mux_a_in),
    .MUX_ALU_A(CU_mux_alu_a), .in(ram_1_data), .IMM(CU_imm), .ALU_SEL(CU_alu_sel), .PC_W_EN(CU_pc_w_en),
    .MUX_PC_IN(CU_mux_pc_in), .W_EN_B(CU_w_en_b), .W_EN_A(CU_w_en_a), .MUX_BR(CU_mux_br),
    .MUX_BR_FINE(CU_mux_br_fine), .W_EN_SP(CU_w_en_sp));
  Multiplexer #(.width(32), .enable("false")) multiplexer_9 (
    .in0(B_out), .in1(A_out), .out(multiplexer_9_out), .sel(CU_mux_mem_in));
  RAM #(.addrWidth(16), .dataWidth(32), .bus("separate")) ram_2 (
    .addr(alu_1_out[15:0]), .din(multiplexer_9_out), .data(ram_2_data), .str(CU_w_en_mem), .clk(clk_out),
    .ld(1'b1), .clr(rst_2_out));  // open: sel

  // Notes on the sheet:
  //   MUX PC IN
  //   MUX BR
  //   MUX A IN
  //   MUX ALU A
  //   MUX ALU B
  //   MUX BR FINE
  //   MUX MEM IN
endmodule

module alu (
  input  [31:0] B,
  input  [31:0] A,
  input  [1:0] code,
  output [31:0] Out,
  output Zero,
  output Neg
);

  wire [31:0] adder_1_out, shifter_1_out, shifter_2_out, subtractor_1_out;

  Adder #(.width(32)) adder_1 (.a(B), .b(A), .out(adder_1_out));  // open: cin, cout
  Subtractor #(.width(32)) subtractor_1 (.a(B), .b(A), .out(subtractor_1_out));  // open: bin, bout
  Shifter #(.width(32)) shifter_1 (.in(B), .\dist (A[4:0]), .out(shifter_1_out));
  Shifter #(.width(32), .shift("lr")) shifter_2 (.in(B), .\dist (A[4:0]), .out(shifter_2_out));
  Multiplexer #(.select(2), .width(32), .enable("false")) multiplexer_1 (
    .in0(adder_1_out), .in1(subtractor_1_out), .in2(shifter_1_out), .in3(shifter_2_out), .out(Out), .sel(code));
  Comparator #(.width(32)) comparator_1 (.a(Out), .b({32{1'b0}}), .eq(Zero), .lt(Neg));  // open: gt
endmodule

module alu_test (
  input  [31:0] in_1,
  input  [31:0] in_2,
  input  [1:0] in_3,
  output [31:0] out_4
);

  wire alu_1_neg, alu_1_zero;

  LED led_1 (.in(alu_1_zero));
  LED led_2 (.in(alu_1_neg));
  alu alu_1 (.code(in_3), .Out(out_4), .Zero(alu_1_zero), .Neg(alu_1_neg), .A(in_1), .B(in_2));
endmodule

module register (
  input  [31:0] in,
  input  wen,
  input  clk,
  input  rst,
  output [31:0] out
);

  Register #(.width(32)) register_1 (.D(in), .en(wen), .Q(out), .clk(clk), .clr(rst));
endmodule

module register_test (
  input  [31:0] in_1,
  input  in_2,
  output [31:0] out_3
);

  wire button_1_out, clock_1_out;

  Button button_1 (.out(button_1_out));
  Clock clock_1 (.out(clock_1_out));
  register register_1 (.in(in_1), .clk(clock_1_out), .wen(in_2), .out(out_3), .rst(button_1_out));
endmodule

// Control Unit
module control_unit (
  input  [31:0] in,
  output [31:0] IMM,
  output MUX_BR,
  output MUX_BR_FINE,
  output [1:0] MUX_ALU_A,
  output W_EN_SP,
  output [1:0] MUX_A_IN,
  output W_EN_B,
  output [1:0] ALU_SEL,
  output W_EN_A,
  output [1:0] MUX_ALU_B,
  output MUX_PC_IN,
  output MUX_MEM_IN,
  output PC_W_EN,
  output W_EN_MEM
);

  wire [7:0] instruction_decoder_1_opcode;

  instruction_decoder instruction_decoder_1 (.in(in), .out_2(IMM), .opcode(instruction_decoder_1_opcode));
  opcode_decoder opcode_decoder_1 (
    .b4(instruction_decoder_1_opcode[4]), .b3(instruction_decoder_1_opcode[3]),
    .b2(instruction_decoder_1_opcode[2]), .b1(instruction_decoder_1_opcode[1]),
    .b0(instruction_decoder_1_opcode[0]), .muxBr(MUX_BR), .wEnB(W_EN_B), .mux_br_fine(MUX_BR_FINE),
    .w_en_sp(W_EN_SP), .mux_mem_in(MUX_MEM_IN), .pc_w_en(PC_W_EN), .wEnA(W_EN_A), .muxAluA1(MUX_ALU_A[1]),
    .muxAluA0(MUX_ALU_A[0]), .muxAluB1(MUX_ALU_B[1]), .muxAluB0(MUX_ALU_B[0]), .muxAIn1(MUX_A_IN[1]),
    .muxAIn0(MUX_A_IN[0]), .muxPcIn(MUX_PC_IN), .aluSel1(ALU_SEL[1]), .aluSel0(ALU_SEL[0]),
    .w_en_mem(W_EN_MEM));
endmodule

module instruction_decoder (
  input  [31:0] in,
  output [31:0] out_2,
  output [7:0] opcode
);

  wire comparator_1_lt;

  Comparator #(.width(24)) comparator_1 (.a(in[31:8]), .b({24{1'b0}}), .lt(comparator_1_lt));  // open: gt, eq
  Multiplexer #(.width(8), .enable("false")) multiplexer_1 (
    .in0({8{1'b0}}), .in1({8{1'b1}}), .out(out_2[31:24]), .sel(comparator_1_lt));

  assign opcode = in[7:0];
  assign out_2[23:0] = in[31:8];
endmodule

// OPCODE DECODER
module opcode_decoder (
  input  b4,
  input  b3,
  input  b2,
  input  b1,
  input  b0,
  output muxBr,
  output wEnB,
  output mux_br_fine,
  output w_en_sp,
  output w_en_mem,
  output mux_mem_in,
  output pc_w_en,
  output wEnA,
  output muxAluA1,
  output muxAluA0,
  output muxAluB1,
  output muxAluB0,
  output muxAIn1,
  output muxAIn0,
  output muxPcIn,
  output aluSel1,
  output aluSel0
);

  wire and_1_out, and_2_out, and_3_out, and_4_out, and_5_out, and_6_out, and_7_out, and_8_out, and_9_out,
       and_10_out, and_11_out, and_12_out, and_13_out, and_14_out, and_15_out, and_16_out, and_17_out,
       and_18_out, and_19_out, and_20_out, and_21_out, and_22_out, and_23_out, and_24_out, and_25_out,
       and_26_out, and_27_out, and_28_out, and_30_out, and_31_out, and_32_out, and_33_out, and_34_out,
       and_35_out, not_1_out, not_2_out, not_3_out, not_4_out, not_5_out, not_6_out, not_7_out, not_8_out,
       not_9_out, not_10_out, not_11_out, not_12_out, not_13_out, not_14_out, not_15_out, not_16_out,
       not_17_out, not_18_out, not_19_out, not_20_out, not_21_out, not_22_out, not_23_out, not_24_out,
       not_25_out, not_26_out, not_27_out, not_28_out, not_29_out, not_30_out, not_31_out, not_32_out,
       not_33_out, not_34_out, not_35_out, not_36_out, not_37_out, not_38_out, not_39_out, not_40_out,
       not_41_out, not_42_out, not_43_out, not_44_out, not_45_out, not_46_out, not_47_out, not_48_out,
       not_49_out, not_50_out, not_51_out, not_52_out, not_53_out, not_54_out, not_55_out, not_56_out,
       not_57_out;

  and and_1 (and_1_out, b3, b2, b0);
  not not_1 (not_1_out, b4);
  not not_2 (not_2_out, b3);
  not not_3 (not_3_out, b2);
  not not_4 (not_4_out, b0);
  not not_5 (not_5_out, b1);
  not not_6 (not_6_out, b4);
  not not_7 (not_7_out, b3);
  not not_8 (not_8_out, b2);
  not not_9 (not_9_out, b4);
  not not_10 (not_10_out, b2);
  not not_11 (not_11_out, b3);
  not not_12 (not_12_out, b0);
  not not_13 (not_13_out, b1);
  not not_14 (not_14_out, b4);
  not not_15 (not_15_out, b3);
  not not_16 (not_16_out, b2);
  not not_17 (not_17_out, b0);
  not not_18 (not_18_out, b3);
  not not_19 (not_19_out, b2);
  not not_20 (not_20_out, b2);
  not not_21 (not_21_out, b0);
  not not_22 (not_22_out, b1);
  not not_23 (not_23_out, b0);
  not not_24 (not_24_out, b4);
  not not_25 (not_25_out, b3);
  not not_26 (not_26_out, b1);
  not not_27 (not_27_out, b2);
  not not_28 (not_28_out, b1);
  not not_29 (not_29_out, b0);
  not not_30 (not_30_out, b2);
  not not_31 (not_31_out, b0);
  not not_32 (not_32_out, b3);
  not not_33 (not_33_out, b2);
  not not_34 (not_34_out, b1);
  not not_35 (not_35_out, b2);
  not not_36 (not_36_out, b1);
  not not_37 (not_37_out, b2);
  not not_38 (not_38_out, b3);
  not not_39 (not_39_out, b1);
  not not_40 (not_40_out, b1);
  not not_41 (not_41_out, b0);
  not not_42 (not_42_out, b2);
  not not_43 (not_43_out, b1);
  not not_44 (not_44_out, b3);
  not not_45 (not_45_out, b2);
  not not_46 (not_46_out, b1);
  or or_1 (muxBr, and_1_out, b4);
  and and_2 (and_2_out, not_1_out, not_2_out, not_3_out, not_4_out);
  and and_3 (and_3_out, b3, b2, not_5_out);
  and and_4 (and_4_out, not_6_out, not_7_out, not_8_out);
  and and_5 (and_5_out, not_9_out, not_10_out, b0);
  and and_6 (and_6_out, not_11_out, b1);
  and and_7 (and_7_out, b2, not_12_out);
  and and_8 (and_8_out, b3, not_13_out);
  and and_9 (and_9_out, not_14_out, not_15_out, not_16_out, not_17_out);
  and and_10 (and_10_out, not_18_out, not_19_out, b1);
  and and_11 (and_11_out, not_20_out, b1, not_21_out);
  and and_12 (and_12_out, b3, b2, not_22_out, not_23_out);
  and and_13 (and_13_out, not_24_out, not_25_out, not_26_out);
  and and_14 (and_14_out, not_27_out, not_28_out, not_29_out);
  and and_15 (and_15_out, b2, b1);
  and and_16 (and_16_out, b3, not_30_out, b0);
  and and_17 (and_17_out, b3, b2, b1, b0);
  and and_18 (and_18_out, b4, not_31_out);
  and and_19 (and_19_out, not_32_out, b2, b1);
  and and_20 (and_20_out, b3, not_33_out, not_34_out);
  and and_21 (and_21_out, not_35_out, not_36_out);
  and and_22 (and_22_out, b2, b1);
  and and_23 (and_23_out, not_37_out, b1);
  and and_24 (and_24_out, not_38_out, b2, not_39_out);
  and and_25 (and_25_out, b3, b1);
  and and_26 (and_26_out, b2, not_40_out, b0);
  and and_27 (and_27_out, b3, b2, b1, not_41_out);
  and and_28 (and_28_out, b4, b0);
  and and_29 (aluSel1, b3, not_42_out, not_43_out);
  and and_30 (and_30_out, not_44_out, b2, b1, b0);
  and and_31 (and_31_out, b3, not_45_out, not_46_out, b0);
  or or_2 (wEnB, and_2_out, and_3_out);
  or or_3 (wEnA, and_4_out, and_5_out, and_6_out, and_7_out, and_8_out);
  or or_4 (muxAluA1, and_9_out, and_10_out, and_11_out, and_12_out);
  or or_5 (muxAluA0, and_13_out, and_14_out, and_15_out, and_16_out);
  or or_6 (muxAluB1, and_17_out, and_18_out);
  or or_7 (muxAluB0, and_19_out, and_20_out);
  or or_8 (muxAIn1, and_21_out, b0, and_22_out, b3);
  or or_9 (muxAIn0, and_23_out, and_24_out, and_25_out);
  or or_10 (muxPcIn, and_26_out, and_27_out, and_28_out);
  or or_11 (aluSel0, and_30_out, and_31_out);
  not not_47 (not_47_out, b2);
  not not_48 (not_48_out, b4);
  and and_32 (and_32_out, not_48_out, b3, not_47_out, b1, not_51_out);
  not not_49 (not_49_out, b4);
  not not_50 (not_50_out, b2);
  not not_51 (not_51_out, b0);
  and and_33 (and_33_out, not_49_out, b3, not_50_out, b1, b0);
  or or_12 (w_en_sp, and_32_out, and_33_out);
  not not_52 (not_52_out, b3);
  not not_53 (not_53_out, b4);
  not not_54 (not_54_out, b2);
  not not_55 (not_55_out, b4);
  and and_34 (and_34_out, not_53_out, not_52_out, not_54_out, b1, b0);
  or or_13 (w_en_mem, and_34_out, and_35_out);
  not not_56 (not_56_out, b1);
  not not_57 (not_57_out, b3);
  and and_35 (and_35_out, not_55_out, not_57_out, b2, not_56_out, b0);

  assign mux_br_fine = b4;
  assign mux_mem_in = b1;
  assign pc_w_en = 1'b1;
endmodule
